// Logisim project Simplified_TTT.circ as structural Verilog: 3 circuits, main circuit main
module main (
);

  wire and_1_out, and_2_out, and_3_out, and_4_out, and_5_out, and_6_out, and_7_out, and_8_out, and_9_out,
       and_10_out, and_11_out, and_12_out, and_33_out, and_34_out, and_35_out, and_36_out, and_37_out,
       and_38_out, and_39_out, and_40_out, and_41_out, button_1_out, button_2_out, button_3_out,
       button_4_out, button_5_out, button_6_out, button_7_out, button_8_out, button_9_out, button_10_out,
       button_11_out, button_12_out, button_13_out, button_14_out, button_15_out, button_16_out,
       button_17_out, button_18_out, button_19_out, button_20_out, clock_1_out, clock_2_out, clock_3_out,
       ILLEGAL_MOVE, MUX0, MUX1, MUX2, MUX3, NO_SPACE, not_1_out, not_2_out, not_3_out, not_4_out, not_5_out,
       not_6_out, not_7_out, not_8_out, not_9_out, not_10_out, not_11_out, not_12_out, not_13_out,
       not_14_out, not_15_out, not_16_out, or_1_out, or_2_out, or_3_out, or_4_out, or_10_out, or_11_out,
       or_12_out, or_13_out, or_14_out, or_15_out, or_16_out, or_17_out, or_18_out, or_19_out, or_20_out,
       or_21_out, or_22_out, or_23_out, or_24_out, or_25_out, or_26_out, or_27_out, or_28_out, P1_en1,
       P1_en2, P1_en3, P1_en4, P1_en5, P1_en6, P1_en7, P1_en8, P1_en9, P1_PLAY, P2_en1, P2_en2, P2_en3,
       P2_en4, P2_en5, P2_en6, P2_en7, P2_en8, P2_en9, P2_PLAY, RESET, TURN, WIN, xor_1_out, xor_2_out,
       xor_3_out;
  wire [1:0] CURRENT_STATE, multiplexer_1_out, multiplexer_2_out, multiplexer_3_out, multiplexer_4_out,
       multiplexer_5_out, multiplexer_6_out, multiplexer_7_out, multiplexer_8_out, multiplexer_9_out,
       multiplexer_10_out, multiplexer_11_out, multiplexer_12_out, multiplexer_13_out, multiplexer_14_out,
       multiplexer_15_out, multiplexer_16_out, multiplexer_17_out, multiplexer_18_out, multiplexer_19_out,
       multiplexer_20_out, multiplexer_21_out, multiplexer_22_out, Position_1_q, Position_2_q, Position_3_q,
       Position_4_q, Position_5_q, Position_6_q, Position_7_q, Position_8_q, Position_9_q,
       Winner_Detector_who;

  not not_1 (not_1_out, ILLEGAL_MOVE);
  not not_2 (not_2_out, ILLEGAL_MOVE);
  Button button_1 (.out(button_1_out));
  Button button_2 (.out(button_2_out));
  Button u_RESET (.out(RESET));
  and and_1 (and_1_out, P1_PLAY, not_1_out);
  and and_2 (and_2_out, P2_PLAY, not_2_out);
  Clock clock_1 (.out(clock_1_out));
  S_R_Flip_Flop s_r_ff_1 (
    .S(and_1_out), .clk(clock_1_out), .R(and_2_out), .Q(TURN), .preset(button_1_out), .reset(button_2_out));  // open: Qn, en
  not not_3 (not_3_out, TURN);
  not not_4 (not_4_out, P2_PLAY);
  not not_5 (not_5_out, P1_PLAY);
  and and_3 (and_3_out, CURRENT_STATE[0], CURRENT_STATE[1]);
  Button button_3 (.out(button_3_out));
  Button button_4 (.out(button_4_out));
  Button button_5 (.out(button_5_out));
  Button button_6 (.out(button_6_out));
  Button button_7 (.out(button_7_out));
  Button button_8 (.out(button_8_out));
  not not_6 (not_6_out, CURRENT_STATE[0]);
  not not_7 (not_7_out, ILLEGAL_MOVE);
  not not_8 (not_8_out, CURRENT_STATE[0]);
  not not_9 (not_9_out, ILLEGAL_MOVE);
  not not_10 (not_10_out, TURN);
  and and_4 (and_4_out, not_10_out, not_11_out);
  not not_11 (not_11_out, and_3_out);
  Button button_9 (.out(button_9_out));
  Button button_10 (.out(button_10_out));
  Button button_11 (.out(button_11_out));
  Button button_12 (.out(button_12_out));
  Button button_13 (.out(button_13_out));
  Button button_14 (.out(button_14_out));
  not not_12 (not_12_out, and_5_out);
  and and_5 (and_5_out, CURRENT_STATE[0], CURRENT_STATE[1]);
  Button button_15 (.out(button_15_out));
  Button button_16 (.out(button_16_out));
  Button button_17 (.out(button_17_out));
  Button button_18 (.out(button_18_out));
  Button button_19 (.out(button_19_out));
  Button button_20 (.out(button_20_out));
  xor xor_1 (xor_1_out, CURRENT_STATE[0], CURRENT_STATE[1]);
  xor xor_2 (xor_2_out, CURRENT_STATE[0], CURRENT_STATE[1]);
  not not_13 (not_13_out, or_1_out);
  or or_1 (or_1_out, CURRENT_STATE[0], CURRENT_STATE[1]);
  or or_2 (or_2_out, not_6_out, CURRENT_STATE[1]);
  or or_3 (or_3_out, CURRENT_STATE[0], CURRENT_STATE[1]);
  not not_14 (not_14_out, or_3_out);
  or or_4 (or_4_out, not_8_out, CURRENT_STATE[1]);
  and and_6 (and_6_out, TURN, not_12_out);
  and and_7 (and_7_out, RESET, not_15_out);
  not not_15 (not_15_out, xor_1_out);
  and and_8 (and_8_out, ILLEGAL_MOVE, xor_2_out);
  and and_9 (and_9_out, not_13_out, P1_PLAY, not_3_out, not_4_out);
  and and_10 (and_10_out, P1_PLAY, not_3_out, or_2_out, not_7_out);
  and and_11 (and_11_out, not_14_out, P2_PLAY, TURN, not_5_out);
  and and_12 (and_12_out, P2_PLAY, TURN, or_4_out, not_9_out);
  or or_5 (P1_PLAY, button_3_out, button_10_out, button_9_out, button_4_out, button_11_out, button_12_out, button_5_out, button_13_out, button_14_out);
  or or_6 (P2_PLAY, button_6_out, button_15_out, button_16_out, button_7_out, button_17_out, button_18_out, button_8_out, button_19_out, button_20_out);
  or or_7 (MUX1, and_9_out, and_10_out);
  or or_8 (MUX2, and_11_out, and_12_out);
  and and_13 (P1_en1, button_3_out, and_4_out);
  and and_14 (P1_en2, button_10_out, and_4_out);
  and and_15 (P1_en3, button_9_out, and_4_out);
  and and_16 (P1_en4, button_4_out, and_4_out);
  and and_17 (P1_en5, button_11_out, and_4_out);
  and and_18 (P1_en6, button_12_out, and_4_out);
  and and_19 (P1_en7, button_5_out, and_4_out);
  and and_20 (P1_en8, button_13_out, and_4_out);
  and and_21 (P1_en9, button_14_out, and_4_out);
  and and_22 (P2_en1, button_6_out, and_6_out);
  and and_23 (P2_en2, button_15_out, and_6_out);
  and and_24 (P2_en3, button_16_out, and_6_out);
  and and_25 (P2_en4, button_7_out, and_6_out);
  and and_26 (P2_en5, button_17_out, and_6_out);
  and and_27 (P2_en6, button_18_out, and_6_out);
  and and_28 (P2_en7, button_8_out, and_6_out);
  and and_29 (P2_en8, button_19_out, and_6_out);
  and and_30 (P2_en9, button_20_out, and_6_out);
  or or_9 (MUX0, and_7_out, and_8_out);
  Multiplexer #(.width(2), .disabled(0), .enable("false")) multiplexer_1 (
    .in0(Position_1_q), .in1(2'b01), .out(multiplexer_1_out), .sel(P1_en1));
  Multiplexer #(.width(2), .disabled(0), .enable("false")) multiplexer_2 (
    .in0(Position_2_q), .in1(2'b01), .out(multiplexer_2_out), .sel(P1_en2));
  Multiplexer #(.width(2), .disabled(0), .enable("false")) multiplexer_3 (
    .in0(Position_3_q), .in1(2'b01), .out(multiplexer_3_out), .sel(P1_en3));
  Multiplexer #(.width(2), .disabled(0), .enable("false")) multiplexer_4 (
    .in0(Position_4_q), .in1(2'b01), .out(multiplexer_4_out), .sel(P1_en4));
  Multiplexer #(.width(2), .disabled(0), .enable("false")) multiplexer_5 (
    .in0(Position_5_q), .in1(2'b01), .out(multiplexer_5_out), .sel(P1_en5));
  Multiplexer #(.width(2), .disabled(0), .enable("false")) multiplexer_6 (
    .in0(Position_6_q), .in1(2'b01), .out(multiplexer_6_out), .sel(P1_en6));
  Multiplexer #(.width(2), .disabled(0), .enable("false")) multiplexer_7 (
    .in0(Position_7_q), .in1(2'b01), .out(multiplexer_7_out), .sel(P1_en7));
  Multiplexer #(.width(2), .disabled(0), .enable("false")) multiplexer_8 (
    .in0(Position_8_q), .in1(2'b01), .out(multiplexer_8_out), .sel(P1_en8));
  Multiplexer #(.width(2), .disabled(0), .enable("false")) multiplexer_9 (
    .in0(Position_9_q), .in1(2'b01), .out(multiplexer_9_out), .sel(P1_en9));
  Multiplexer #(.width(2), .disabled(0), .enable("false")) multiplexer_10 (
    .in0(multiplexer_1_out), .in1(2'b10), .out(multiplexer_10_out), .sel(P2_en1));
  Multiplexer #(.width(2), .disabled(0), .enable("false")) multiplexer_11 (
    .in0(multiplexer_2_out), .in1(2'b10), .out(multiplexer_11_out), .sel(P2_en2));
  Multiplexer #(.width(2), .disabled(0), .enable("false")) multiplexer_12 (
    .in0(multiplexer_3_out), .in1(2'b10), .out(multiplexer_12_out), .sel(P2_en3));
  Multiplexer #(.width(2), .disabled(0), .enable("false")) multiplexer_13 (
    .in0(multiplexer_4_out), .in1(2'b10), .out(multiplexer_13_out), .sel(P2_en4));
  Multiplexer #(.width(2), .disabled(0), .enable("false")) multiplexer_14 (
    .in0(multiplexer_5_out), .in1(2'b10), .out(multiplexer_14_out), .sel(P2_en5));
  Multiplexer #(.width(2), .disabled(0), .enable("false")) multiplexer_15 (
    .in0(multiplexer_6_out), .in1(2'b10), .out(multiplexer_15_out), .sel(P2_en6));
  Multiplexer #(.width(2), .disabled(0), .enable("false")) multiplexer_16 (
    .in0(multiplexer_7_out), .in1(2'b10), .out(multiplexer_16_out), .sel(P2_en7));
  Multiplexer #(.width(2), .disabled(0), .enable("false")) multiplexer_17 (
    .in0(multiplexer_8_out), .in1(2'b10), .out(multiplexer_17_out), .sel(P2_en8));
  Multiplexer #(.width(2), .disabled(0), .enable("false")) multiplexer_18 (
    .in0(multiplexer_9_out), .in1(2'b10), .out(multiplexer_18_out), .sel(P2_en9));
  xor xor_3 (xor_3_out, CURRENT_STATE[0], CURRENT_STATE[1]);
  or or_10 (or_10_out, WIN, NO_SPACE);
  not not_16 (not_16_out, ILLEGAL_MOVE);
  Clock clock_2 (.out(clock_2_out));
  and and_31 (MUX3, xor_3_out, or_10_out);
  Register #(.width(2)) Position_1 (
    .D(multiplexer_10_out), .en(not_16_out), .Q(Position_1_q), .clk(clock_2_out), .clr(RESET));
  Register #(.width(2)) Position_2 (
    .D(multiplexer_11_out), .en(not_16_out), .Q(Position_2_q), .clk(clock_2_out), .clr(RESET));
  Register #(.width(2)) Position_3 (
    .D(multiplexer_12_out), .en(not_16_out), .Q(Position_3_q), .clk(clock_2_out), .clr(RESET));
  Register #(.width(2)) Position_4 (
    .D(multiplexer_13_out), .en(not_16_out), .Q(Position_4_q), .clk(clock_2_out), .clr(RESET));
  Register #(.width(2)) Position_5 (
    .D(multiplexer_14_out), .en(not_16_out), .Q(Position_5_q), .clk(clock_2_out), .clr(RESET));
  Register #(.width(2)) Position_6 (
    .D(multiplexer_15_out), .en(not_16_out), .Q(Position_6_q), .clk(clock_2_out), .clr(RESET));
  Register #(.width(2)) Position_7 (
    .D(multiplexer_16_out), .en(not_16_out), .Q(Position_7_q), .clk(clock_2_out), .clr(RESET));
  Register #(.width(2)) Position_8 (
    .D(multiplexer_17_out), .en(not_16_out), .Q(Position_8_q), .clk(clock_2_out), .clr(RESET));
  Register #(.width(2)) Position_9 (
    .D(multiplexer_18_out), .en(not_16_out), .Q(Position_9_q), .clk(clock_2_out), .clr(RESET));
  Multiplexer #(.width(2), .disabled(0), .enable("false")) multiplexer_19 (
    .in0(CURRENT_STATE), .in1(2'b11), .out(multiplexer_19_out), .sel(MUX3));
  Multiplexer #(.width(2), .disabled(0), .enable("false")) multiplexer_20 (
    .in0(multiplexer_19_out), .in1(2'b10), .out(multiplexer_20_out), .sel(MUX2));
  Multiplexer #(.width(2), .disabled(0), .enable("false")) multiplexer_21 (
    .in0(multiplexer_20_out), .in1(2'b00), .out(multiplexer_21_out), .sel(MUX0));
  Multiplexer #(.width(2), .disabled(0), .enable("false")) multiplexer_22 (
    .in0(multiplexer_21_out), .in1(2'b01), .out(multiplexer_22_out), .sel(MUX1));
  Clock clock_3 (.out(clock_3_out));
  Winner_Detector Winner_Detector (
    .in_1(Position_1_q), .in_2(Position_2_q), .in_3(Position_3_q), .in_4(Position_4_q), .in_5(Position_5_q),
    .in_6(Position_6_q), .in_7(Position_7_q), .in_8(Position_8_q), .in_9(Position_9_q), .wi(WIN),
    .who(Winner_Detector_who));
  Hex_Digit_Display hex_digit_display_1 (.value({2'b00, CURRENT_STATE}));  // open: dp
  Register #(.width(2)) FSM_STATES (
    .D(multiplexer_22_out), .Q(CURRENT_STATE), .clk(clock_3_out), .clr(RESET));  // open: en
  or or_11 (or_11_out, Position_1_q[0], Position_1_q[1]);
  or or_12 (or_12_out, Position_2_q[0], Position_2_q[1]);
  or or_13 (or_13_out, Position_3_q[0], Position_3_q[1]);
  or or_14 (or_14_out, Position_4_q[0], Position_4_q[1]);
  or or_15 (or_15_out, Position_5_q[0], Position_5_q[1]);
  or or_16 (or_16_out, Position_6_q[0], Position_6_q[1]);
  or or_17 (or_17_out, Position_7_q[0], Position_7_q[1]);
  or or_18 (or_18_out, Position_8_q[0], Position_8_q[1]);
  or or_19 (or_19_out, Position_9_q[0], Position_9_q[1]);
  LED led_1 (.in(Position_1_q[0]));
  LED led_2 (.in(Position_1_q[1]));
  LED led_3 (.in(Position_4_q[0]));
  LED led_4 (.in(Position_4_q[1]));
  LED led_5 (.in(Position_7_q[0]));
  LED led_6 (.in(Position_7_q[1]));
  LED led_7 (.in(Winner_Detector_who[0]));
  LED led_8 (.in(Winner_Detector_who[1]));
  LED led_9 (.in(NO_SPACE));
  LED led_10 (.in(Position_2_q[0]));
  LED led_11 (.in(Position_2_q[1]));
  LED led_12 (.in(Position_5_q[0]));
  LED led_13 (.in(Position_5_q[1]));
  LED led_14 (.in(Position_8_q[0]));
  LED led_15 (.in(Position_8_q[1]));
  and and_32 (NO_SPACE, or_11_out, or_12_out, or_13_out, or_14_out, or_15_out, or_16_out, or_17_out, or_18_out, or_19_out);
  LED led_16 (.in(Position_3_q[0]));
  LED led_17 (.in(Position_3_q[1]));
  LED led_18 (.in(Position_6_q[0]));
  LED led_19 (.in(Position_6_q[1]));
  LED led_20 (.in(Position_9_q[0]));
  LED led_21 (.in(Position_9_q[1]));
  or or_20 (or_20_out, P1_en1, P2_en1);
  or or_21 (or_21_out, P2_en2, P1_en2);
  or or_22 (or_22_out, P2_en3, P1_en3);
  or or_23 (or_23_out, P2_en4, P1_en4);
  or or_24 (or_24_out, P2_en5, P1_en5);
  or or_25 (or_25_out, P2_en6, P1_en6);
  or or_26 (or_26_out, P2_en7, P1_en7);
  or or_27 (or_27_out, P2_en8, P1_en8);
  or or_28 (or_28_out, P2_en9, P1_en9);
  and and_33 (and_33_out, or_20_out, or_11_out);
  and and_34 (and_34_out, or_12_out, or_21_out);
  and and_35 (and_35_out, or_13_out, or_22_out);
  and and_36 (and_36_out, or_14_out, or_23_out);
  and and_37 (and_37_out, or_15_out, or_24_out);
  and and_38 (and_38_out, or_16_out, or_25_out);
  and and_39 (and_39_out, or_17_out, or_26_out);
  and and_40 (and_40_out, or_18_out, or_27_out);
  and and_41 (and_41_out, or_19_out, or_28_out);
  or or_29 (ILLEGAL_MOVE, and_33_out, and_34_out, and_35_out, and_36_out, and_37_out, and_38_out, and_39_out, and_40_out, and_41_out);

  // Notes on the sheet:
  //   PLAYER 2
  //   PLAYER 1
  //   WHO'S FIRST ?
  //   PLAYER 2
  //   PLAYER 1
  //   Winner is
  //   Player 1
  //   Player 2
  //   Draw
endmodule

module _1_case_winner_detect (
  input  [1:0] in_1,
  input  [1:0] in_2,
  input  [1:0] in_3,
  output winner,
  output [1:0] Who
);

  wire or_1_out;
  wire [1:0] and_1_out, xnor_1_out, xnor_2_out;

  assign xnor_1_out = ~(in_1 ^ in_2);  // XNOR_Gate xnor_1, 2 bits wide
  assign xnor_2_out = ~(in_2 ^ in_3);  // XNOR_Gate xnor_2, 2 bits wide
  or or_1 (or_1_out, in_1[0], in_1[1]);
  assign and_1_out = xnor_1_out & xnor_2_out;  // AND_Gate and_1, 2 bits wide
  and and_2 (winner, and_1_out[0], and_1_out[1], or_1_out);
  assign Who = {2{winner}} & in_3;  // AND_Gate and_3, 2 bits wide
endmodule

module Winner_Detector (
  input  [1:0] in_1,
  input  [1:0] in_2,
  input  [1:0] in_3,
  input  [1:0] in_4,
  input  [1:0] in_5,
  input  [1:0] in_6,
  input  [1:0] in_7,
  input  [1:0] in_8,
  input  [1:0] in_9,
  output wi,
  output [1:0] who
);

  wire n1_case_winner_detect_1_winner, n1_case_winner_detect_2_winner, n1_case_winner_detect_3_winner,
       n1_case_winner_detect_4_winner, n1_case_winner_detect_5_winner, n1_case_winner_detect_6_winner,
       n1_case_winner_detect_7_winner, n1_case_winner_detect_8_winner;
  wire [1:0] n1_case_winner_detect_1_who, n1_case_winner_detect_2_who, n1_case_winner_detect_3_who,
       n1_case_winner_detect_4_who, n1_case_winner_detect_5_who, n1_case_winner_detect_6_who,
       n1_case_winner_detect_7_who, n1_case_winner_detect_8_who;

  _1_case_winner_detect u_1_case_winner_detect_1 (
    .in_1(in_1), .in_2(in_2), .in_3(in_3), .winner(n1_case_winner_detect_1_winner),
    .Who(n1_case_winner_detect_1_who));
  _1_case_winner_detect u_1_case_winner_detect_2 (
    .in_1(in_4), .in_2(in_5), .in_3(in_6), .winner(n1_case_winner_detect_2_winner),
    .Who(n1_case_winner_detect_2_who));
  _1_case_winner_detect u_1_case_winner_detect_3 (
    .in_1(in_7), .in_2(in_8), .in_3(in_9), .winner(n1_case_winner_detect_3_winner),
    .Who(n1_case_winner_detect_3_who));
  _1_case_winner_detect u_1_case_winner_detect_4 (
    .in_1(in_1), .in_2(in_4), .in_3(in_7), .winner(n1_case_winner_detect_4_winner),
    .Who(n1_case_winner_detect_4_who));
  _1_case_winner_detect u_1_case_winner_detect_5 (
    .in_1(in_2), .in_2(in_5), .in_3(in_8), .winner(n1_case_winner_detect_5_winner),
    .Who(n1_case_winner_detect_5_who));
  _1_case_winner_detect u_1_case_winner_detect_6 (
    .in_1(in_3), .in_2(in_6), .in_3(in_9), .winner(n1_case_winner_detect_6_winner),
    .Who(n1_case_winner_detect_6_who));
  _1_case_winner_detect u_1_case_winner_detect_7 (
    .in_1(in_1), .in_2(in_5), .in_3(in_9), .winner(n1_case_winner_detect_7_winner),
    .Who(n1_case_winner_detect_7_who));
  _1_case_winner_detect u_1_case_winner_detect_8 (
    .in_1(in_3), .in_2(in_5), .in_3(in_7), .winner(n1_case_winner_detect_8_winner),
    .Who(n1_case_winner_detect_8_who));
  or or_1 (wi, n1_case_winner_detect_1_winner, n1_case_winner_detect_2_winner, n1_case_winner_detect_3_winner, n1_case_winner_detect_4_winner, n1_case_winner_detect_5_winner, n1_case_winner_detect_6_winner, n1_case_winner_detect_7_winner, n1_case_winner_detect_8_winner);
  assign who = n1_case_winner_detect_1_who | n1_case_winner_detect_2_who | n1_case_winner_detect_3_who | n1_case_winner_detect_4_who | n1_case_winner_detect_5_who | n1_case_winner_detect_6_who | n1_case_winner_detect_7_who | n1_case_winner_detect_8_who;  // OR_Gate or_2, 2 bits wide
endmodule
